# Fritzing sketch BLETempSensor (saved by Fritzing 0.9.4)
breadboards: 1

parts:
  U1 = attiny85 [package=dip]
  V1 = DC Power [voltage=3.7V]
  R1 = Temperature Sensor (Thermistor) [thermistor_type=NTC package=THT]
  R2 = Resistor [tolerance=±5% resistance=10k package=THT]

nets:
  N1: U1.Pin_2, R1.pin_0, R2.Pin_0
  Charger -/HM-10 GND: U1.Pin_4, V1.V-, R2.Pin_1
  HM-10 TX: U1.Pin_5
  HM-10 RX: U1.Pin_6
  Charger +/HM-10 Vcc: V1.V+, R1.pin_1

notes:
  BLE Therometor Schematic
